// Logisim project maquina.circ as structural Verilog: 2 circuits, main circuit somador
module somador (
  input  in_1,
  input  in_2,
  input  in_3,
  input  in_4,
  input  in_5,
  input  in_6,
  output out_7
);

  wire button_1_out, comparator_1_eq, comparator_1_gt, n7_segment_display_2_p1, or_3_out, or_4_out;
  wire [1:0] or_1_out;
  wire [3:0] binary_to_bcd_converter_1_p3;
  wire [5:0] adder_1_out, multiplexer_1_out, multiplexer_2_out, register_1_q, register_2_q;

  or or_1 (or_1_out[0], in_2, in_4);
  or or_2 (or_1_out[1], in_4, in_3);
  Multiplexer #(.select(3), .width(6)) multiplexer_1 (
    .in0({{5{1'b0}}, in_1}), .in1({4'b0000, in_2, 1'b0}), .in2({4'b0000, {2{in_3}}}),
    .in3({3'b000, in_4, 1'b0, in_4}), .in4({3'b000, {3{in_5}}}), .out(multiplexer_1_out),
    .sel({in_5, or_1_out}));  // open: in5, in6, in7
  or or_3 (or_3_out, in_1, in_2, in_3, in_4, in_5);
  or or_4 (or_4_out, or_3_out, in_6);
  Adder #(.width(6)) adder_1 (.a(register_1_q), .b(multiplexer_1_out), .out(adder_1_out));  // open: cin, cout
  Multiplexer #(.width(6)) multiplexer_2 (.in0(adder_1_out), .in1(register_2_q), .out(multiplexer_2_out), .sel(in_6));
  Register #(.trigger("falling"), .width(6)) register_1 (
    .D(multiplexer_2_out), .clk(or_4_out), .Q(register_1_q), .clr(button_1_out));  // open: en
  Register #(.trigger("falling"), .width(6)) register_2 (
    .D(register_1_q), .clk(or_4_out), .Q(register_2_q), .clr(button_1_out));  // open: en
  Button button_1 (.out(button_1_out));
  _7_Segment_Display u_7_segment_display_1 ();  // open: g, f, a, b, e, d, c, dp
  // _7_Segment_Display 7_segment_display_2: pin names not known; wires that end beside it: n7_segment_display_2_p1, n7_segment_display_2_p1
  // BCD_to_7_Segment_decoder bcd_to_7_segment_decoder_1: pin names not known
  // BCD_to_7_Segment_decoder bcd_to_7_segment_decoder_2: pin names not known
  // Binary_to_BCD_converter #(.binvalue(6)) binary_to_bcd_converter_1: pin names not known; wires that end beside it: or_4_out, register_1_q, binary_to_bcd_converter_1_p3
  Comparator #(.width(4)) comparator_1 (
    .a(binary_to_bcd_converter_1_p3), .b(4'b0101), .gt(comparator_1_gt), .eq(comparator_1_eq));  // open: lt
  or or_5 (out_7, comparator_1_gt, comparator_1_eq);
endmodule

module estados (
);

  wire and_1_out, and_2_out, and_3_out, and_4_out, and_5_out, and_6_out, and_7_out, and_8_out, and_9_out,
       and_10_out, and_11_out, and_12_out, and_13_out, and_14_out, and_15_out, and_16_out, button_1_out,
       button_2_out, button_3_out, button_4_out, button_5_out, button_6_out, button_7_out, not_1_out,
       not_2_out, not_3_out, not_4_out, not_5_out, not_6_out, not_7_out, not_8_out, not_9_out, not_10_out,
       not_11_out, not_12_out, not_13_out, not_14_out, not_15_out, not_16_out, not_17_out, not_18_out,
       not_19_out, not_20_out, not_21_out, or_1_out, or_2_out, or_3_out, or_4_out, or_5_out, or_6_out,
       or_7_out, or_8_out, register_1_q, register_2_q, register_3_q, somador_1_out_7;

  not not_1 (not_1_out, register_3_q);
  not not_2 (not_2_out, button_5_out);
  not not_3 (not_3_out, button_7_out);
  not not_4 (not_4_out, button_3_out);
  not not_5 (not_5_out, button_7_out);
  not not_6 (not_6_out, button_3_out);
  not not_7 (not_7_out, button_5_out);
  not not_8 (not_8_out, button_5_out);
  not not_9 (not_9_out, button_4_out);
  not not_10 (not_10_out, button_6_out);
  not not_11 (not_11_out, button_7_out);
  and and_1 (and_1_out, not_1_out, register_2_q);
  and and_2 (and_2_out, button_4_out, not_8_out);
  and and_3 (and_3_out, button_5_out, not_9_out);
  and and_4 (and_4_out, not_10_out, button_7_out);
  and and_5 (and_5_out, not_11_out, button_6_out);
  not not_12 (not_12_out, register_2_q);
  and and_6 (and_6_out, button_3_out, not_2_out, not_3_out);
  and and_7 (and_7_out, not_4_out, button_5_out, not_5_out);
  and and_8 (and_8_out, not_6_out, not_7_out, button_7_out);
  or or_1 (or_1_out, and_1_out, not_12_out);
  or or_2 (or_2_out, and_4_out, and_5_out);
  Button button_1 (.out(button_1_out));
  or or_3 (or_3_out, and_2_out, and_3_out);
  or or_4 (or_4_out, and_6_out, and_7_out, and_8_out);
  not not_13 (not_13_out, button_6_out);
  not not_14 (not_14_out, button_7_out);
  and and_9 (and_9_out, or_1_out, register_1_q);
  not not_15 (not_15_out, button_2_out);
  not not_16 (not_16_out, button_3_out);
  not not_17 (not_17_out, button_4_out);
  not not_18 (not_18_out, button_5_out);
  not not_19 (not_19_out, somador_1_out_7);
  not not_20 (not_20_out, register_1_q);
  or or_5 (or_5_out, somador_1_out_7, register_1_q);
  and and_10 (and_10_out, not_15_out, not_16_out, not_13_out, not_14_out, not_19_out, or_3_out);
  and and_11 (and_11_out, not_15_out, not_16_out, not_17_out, not_18_out, not_19_out, or_2_out);
  or or_6 (or_6_out, and_9_out, not_20_out);
  or or_7 (or_7_out, somador_1_out_7, register_2_q);
  LED led_1 (.in(or_5_out));
  LED led_2 (.in(or_7_out));
  and and_12 (and_12_out, not_15_out, not_17_out, not_13_out, not_19_out, or_4_out);
  LED led_3 (.in(register_3_q));
  and and_13 (and_13_out, and_10_out, or_6_out);
  or or_8 (or_8_out, button_3_out, button_4_out, button_5_out, button_6_out, button_7_out, button_2_out);
  and and_14 (and_14_out, and_11_out, or_6_out);
  Register #(.trigger("high"), .width(1)) register_1 (
    .D(and_14_out), .clk(or_8_out), .Q(register_1_q), .clr(button_1_out));  // open: en
  and and_15 (and_15_out, and_12_out, or_6_out);
  Register #(.trigger("high"), .width(1)) register_2 (
    .D(and_13_out), .clk(or_8_out), .Q(register_2_q), .clr(button_1_out));  // open: en
  Register #(.trigger("high"), .width(1)) register_3 (
    .D(and_15_out), .clk(or_8_out), .Q(register_3_q), .clr(button_1_out));  // open: en
  not not_21 (not_21_out, register_3_q);
  Button button_2 (.out(button_2_out));
  Button button_3 (.out(button_3_out));
  Button button_4 (.out(button_4_out));
  Button button_5 (.out(button_5_out));
  Button button_6 (.out(button_6_out));
  Button button_7 (.out(button_7_out));
  somador somador_1 (
    .in_1(button_3_out), .in_2(button_4_out), .in_3(button_5_out), .in_4(button_6_out), .in_5(button_7_out),
    .in_6(button_2_out), .out_7(somador_1_out_7));
  and and_16 (and_16_out, or_5_out, or_7_out, not_21_out, somador_1_out_7);
  LED led_4 (.in(and_16_out));

  // Notes on the sheet:
  //   reset
  //   e0'
  //   e1'
  //   e2'
  //   e0
  //   e1
  //   u
  //   e2
  //   1
  //   2
  //   3
  //   5
  //   7
  //   v
endmodule
