// Logisim project placartrabalho.circ as structural Verilog: 3 circuits, main circuit main
module main (
);

  wire bcd_to_7_segment_decoder_2_p1, button_1_out, button_2_out, button_3_out, button_4_out, button_5_out,
       button_6_out, comparador_1_out_2;
  wire [3:0] binary_to_bcd_converter_1_p2;
  wire [5:0] somador_1_soma;

  Button button_1 (.out(button_1_out));
  Button button_2 (.out(button_2_out));
  Button button_3 (.out(button_3_out));
  Button button_4 (.out(button_4_out));
  Button button_5 (.out(button_5_out));
  Button button_6 (.out(button_6_out));
  LED led_1 (.in(comparador_1_out_2));
  comparador comparador_1 (.dezena(binary_to_bcd_converter_1_p2), .out_2(comparador_1_out_2));
  somador somador_1 (
    .plus_1(button_1_out), .plus_2(button_2_out), .plus_3(button_3_out), .plus_5(button_4_out),
    .plus_7(button_5_out), .undo(button_6_out), .soma(somador_1_soma));
  _7_Segment_Display u_7_segment_display_1 ();  // open: g, f, a, b, e, d, c, dp
  _7_Segment_Display u_7_segment_display_2 ();  // open: g, f, a, b, e, d, c, dp
  // BCD_to_7_Segment_decoder bcd_to_7_segment_decoder_1: pin names not known
  // BCD_to_7_Segment_decoder bcd_to_7_segment_decoder_2: pin names not known; wires that end beside it: bcd_to_7_segment_decoder_2_p1
  // Binary_to_BCD_converter #(.binvalue(6)) binary_to_bcd_converter_1: pin names not known; wires that end beside it: somador_1_soma, binary_to_bcd_converter_1_p2, binary_to_bcd_converter_1_p2, bcd_to_7_segment_decoder_2_p1

  // Notes on the sheet:
  //   botões
  //   de
  //   soma
  //   1
  //   2
  //   3
  //   5
  //   7
  //   U
  //   undo
  //   led que indica
  //   o fim do jogo
  //   comparador
  //   soma total
  //   decodificador (1)
  //   decodificador (2) 
  //   + placar
endmodule

module somador (
  input  plus_1,
  input  plus_2,
  input  plus_3,
  input  plus_5,
  input  plus_7,
  input  undo,
  output [5:0] soma
);

  wire button_1_out, or_3_out, or_4_out;
  wire [1:0] or_1_out;
  wire [5:0] adder_1_out, multiplexer_1_out, multiplexer_2_out, register_2_q;

  or or_1 (or_1_out[0], plus_2, plus_5);
  or or_2 (or_1_out[1], plus_5, plus_3);
  Multiplexer #(.select(3), .width(6)) multiplexer_1 (
    .in0({{5{1'b0}}, plus_1}), .in1({4'b0000, plus_2, 1'b0}), .in2({4'b0000, {2{plus_3}}}),
    .in3({3'b000, plus_5, 1'b0, plus_5}), .in4({3'b000, {3{plus_7}}}), .out(multiplexer_1_out),
    .sel({plus_7, or_1_out}));  // open: in5, in6, in7
  or or_3 (or_3_out, or_1_out[0], or_1_out[1], plus_7, plus_1);
  Adder #(.width(6)) adder_1 (.a(soma), .b(multiplexer_1_out), .out(adder_1_out));  // open: cin, cout
  Multiplexer #(.width(6)) multiplexer_2 (.in0(adder_1_out), .in1(register_2_q), .out(multiplexer_2_out), .sel(undo));
  or or_4 (or_4_out, undo, or_3_out);
  Register #(.trigger("falling"), .width(6)) register_1 (
    .D(multiplexer_2_out), .clk(or_4_out), .Q(soma), .clr(button_1_out));  // open: en
  Register #(.trigger("falling"), .width(6)) register_2 (
    .D(soma), .clk(or_3_out), .Q(register_2_q), .clr(button_1_out));  // open: en
  Button button_1 (.out(button_1_out));

  // Notes on the sheet:
  //   botões
  //   de
  //   soma
  //   variáveis de controle
  //   distribuição dos bits
  //   seleção 1
  //   clock
  //   somador
  //   clock
  //   seleção 2
  //   valor
  //   atual
  //   valor
  //   antigo
  //   reset
endmodule

module comparador (
  input  [3:0] dezena,
  output out_2
);

  wire comparator_1_eq, comparator_1_gt;

  Comparator #(.width(4)) comparator_1 (
    .a(dezena), .b(4'b0101), .gt(comparator_1_gt), .eq(comparator_1_eq));  // open: lt
  or or_1 (out_2, comparator_1_gt, comparator_1_eq);
endmodule
