// Logisim project isatrabalho.circ as structural Verilog: 3 circuits, main circuit main
module main (
);

  wire beq, bge, bne, button_2_out, button_3_out, clk, comparator_2_eq, comparator_2_gt, controlers2rd,
       mux_ula, or_1_out, or_3_out, reset_pc_and_reg, wbreg, wm;
  wire [1:0] controledado, pccontrol;
  wire [2:0] multiplexer_6_out, multiplexer_7_out, opcodeula, rd, rs1_t, rs2_t;
  wire [3:0] opcode;
  wire [4:0] rom_1_data;
  wire [17:0] adder_1_out, imm, multiplexer_1_out, multiplexer_2_out, multiplexer_3_out, multiplexer_4_out,
       multiplexer_5_out, multiplexer_8_out, multiplexer_9_out, PC_q, pcmaisimm, pcmaisum, ram_1_dout,
       registradores_1_saidard, Rs1, Rs2, ula_1_out_5;

  Clock clock_1 (.out(clk));
  Adder #(.width(18)) adder_1 (.a(imm), .b(Rs1), .out(adder_1_out));  // open: cin, cout
  Button button_1 (.out(reset_pc_and_reg));
  Multiplexer #(.width(18)) multiplexer_1 (.in0(pcmaisum), .in1(pcmaisimm), .out(multiplexer_1_out), .sel(beq));
  Multiplexer #(.select(2), .width(18)) multiplexer_2 (
    .in0(pcmaisum), .in1(pcmaisimm), .in2(multiplexer_3_out), .in3(adder_1_out), .out(multiplexer_2_out),
    .sel(pccontrol));
  Multiplexer #(.select(2), .width(18)) multiplexer_3 (
    .in1(multiplexer_1_out), .in2(multiplexer_4_out), .in3(multiplexer_5_out), .out(multiplexer_3_out),
    .sel(opcode[1:0]));  // open: in0
  Multiplexer #(.width(18)) multiplexer_4 (.in0(pcmaisum), .in1(pcmaisimm), .out(multiplexer_4_out), .sel(bge));
  not not_1 (bne, beq);
  Register #(.width(18)) PC (.D(multiplexer_2_out), .en(1'b1), .clk(clk), .Q(PC_q), .clr(or_1_out));
  or or_1 (or_1_out, button_2_out, reset_pc_and_reg);
  Button button_2 (.out(button_2_out));
  Comparator #(.width(18)) comparator_1 (.a(Rs1), .b(Rs2), .eq(beq));  // open: gt, lt
  Adder #(.width(18)) adder_2 (.a(PC_q), .b(18'h1), .out(pcmaisum));  // open: cin, cout
  Adder #(.width(18)) adder_3 (.a(PC_q), .b(imm), .out(pcmaisimm));  // open: cin, cout
  Multiplexer #(.width(18)) multiplexer_5 (.in0(pcmaisum), .in1(pcmaisimm), .out(multiplexer_5_out), .sel(bne));
  ROM #(.addrWidth(18), .dataWidth(18)) rom_1 (.addr(PC_q), .data({opcode, rd, rs1_t, rs2_t, rom_1_data}));
  Comparator #(.width(18)) comparator_2 (.a(Rs2), .b(Rs1), .gt(comparator_2_gt), .eq(comparator_2_eq));  // open: lt
  or or_2 (bge, comparator_2_gt, comparator_2_eq);
  assign imm = {{10{rs2_t[2]}}, {rs2_t, rom_1_data}};  // Bit_Extender bit_extender_1
  Multiplexer #(.width(3)) multiplexer_6 (.in0(rd), .in1(rs2_t), .out(multiplexer_6_out), .sel(controlers2rd));
  Multiplexer #(.width(3)) multiplexer_7 (.in0(rs2_t), .in1(rd), .out(multiplexer_7_out), .sel(controlers2rd));
  Button button_3 (.out(button_3_out));
  or or_3 (or_3_out, button_3_out, reset_pc_and_reg);
  registradores registradores_1 (
    .dado(multiplexer_8_out), .rs1(rs1_t), .rs2(multiplexer_7_out), .rd(multiplexer_6_out), .w(wbreg),
    .clk(clk), .reset(or_3_out), .saidars1(Rs1), .saidars2(Rs2), .saidard(registradores_1_saidard));
  ROM #(.addrWidth(4), .dataWidth(11)) rom_2 (
    .addr(opcode), .data({pccontrol, wbreg, mux_ula, controledado, wm, opcodeula, controlers2rd}));
  Multiplexer #(.select(2), .width(18)) multiplexer_8 (
    .in0(ula_1_out_5), .in1(ram_1_dout), .in2(pcmaisum), .out(multiplexer_8_out), .sel(controledado));  // open: in3
  Multiplexer #(.width(18)) multiplexer_9 (.in0(Rs2), .in1(imm), .out(multiplexer_9_out), .sel(mux_ula));
  ULA ula_1 (
    .rs1(Rs1), .rs2(multiplexer_9_out), .rd(registradores_1_saidard), .opcodeula(opcodeula),
    .out_5(ula_1_out_5));
  RAM #(.addrWidth(18), .dataWidth(18)) ram_1 (
    .addr(ula_1_out_5), .we(wm), .oe(1'b1), .clk(clk), .din(registradores_1_saidard), .dout(ram_1_dout));

  // Notes on the sheet:
  //   contents of rom_1 (hex, n*v repeats v):
  //   8804 9005 20920 21240 14a04 19106 5*0 1d103 0 0 9808 2d940 25940 29940 39940 3da20 8802 14b02 0
  //   18a06 1d903 31a20 35a20 c803 0 0 1110c 11*0 5101 901
  //   contents of rom_2 (hex, n*v repeats v):
  //   1a0 90 180 340 340 401 401 401 100 102 104 106 108 10a 10c 10e
endmodule

module registradores (
  input  [17:0] dado,
  input  [2:0] rs1,
  input  [2:0] rs2,
  input  [2:0] rd,
  input  w,
  input  clk,
  input  reset,
  output [17:0] saidars1,
  output [17:0] saidars2,
  output [17:0] saidard
);

  wire demultiplexer_1_out1, demultiplexer_1_out2, demultiplexer_1_out3, demultiplexer_1_out4,
       demultiplexer_1_out5, demultiplexer_1_out6, demultiplexer_1_out7;
  wire [17:0] multiplexer_1_out, multiplexer_2_out, multiplexer_3_out, multiplexer_4_out, multiplexer_5_out,
       multiplexer_6_out, multiplexer_7_out, vr1, vr2, vr3, vr4, vr5, vr6, vr7;

  Demultiplexer #(.select(3)) demultiplexer_1 (
    .out1(demultiplexer_1_out1), .out2(demultiplexer_1_out2), .out3(demultiplexer_1_out3),
    .out4(demultiplexer_1_out4), .out5(demultiplexer_1_out5), .out6(demultiplexer_1_out6),
    .out7(demultiplexer_1_out7), .in(w), .sel(rd));  // open: out0
  Multiplexer #(.width(18)) multiplexer_1 (.in0(vr1), .in1(dado), .out(multiplexer_1_out), .sel(demultiplexer_1_out1));
  Multiplexer #(.width(18)) multiplexer_2 (.in0(vr2), .in1(dado), .out(multiplexer_2_out), .sel(demultiplexer_1_out2));
  Multiplexer #(.width(18)) multiplexer_3 (.in0(vr3), .in1(dado), .out(multiplexer_3_out), .sel(demultiplexer_1_out3));
  Multiplexer #(.width(18)) multiplexer_4 (.in0(vr4), .in1(dado), .out(multiplexer_4_out), .sel(demultiplexer_1_out4));
  Multiplexer #(.width(18)) multiplexer_5 (.in0(vr5), .in1(dado), .out(multiplexer_5_out), .sel(demultiplexer_1_out5));
  Multiplexer #(.width(18)) multiplexer_6 (.in0(vr6), .in1(dado), .out(multiplexer_6_out), .sel(demultiplexer_1_out6));
  Multiplexer #(.width(18)) multiplexer_7 (.in0(vr7), .in1(dado), .out(multiplexer_7_out), .sel(demultiplexer_1_out7));
  Register #(.width(18)) r1 (.D(multiplexer_1_out), .clk(clk), .Q(vr1), .clr(reset));  // open: en
  Register #(.width(18)) r2 (.D(multiplexer_2_out), .clk(clk), .Q(vr2), .clr(reset));  // open: en
  Register #(.width(18)) r3 (.D(multiplexer_3_out), .clk(clk), .Q(vr3), .clr(reset));  // open: en
  Register #(.width(18)) r4 (.D(multiplexer_4_out), .clk(clk), .Q(vr4), .clr(reset));  // open: en
  Register #(.width(18)) r5 (.D(multiplexer_5_out), .clk(clk), .Q(vr5), .clr(reset));  // open: en
  Register #(.width(18)) r6 (.D(multiplexer_6_out), .clk(clk), .Q(vr6), .clr(reset));  // open: en
  Register #(.width(18)) r7 (.D(multiplexer_7_out), .clk(clk), .Q(vr7), .clr(reset));  // open: en
  Multiplexer #(.select(3), .width(18)) multiplexer_8 (
    .in0({18{1'b0}}), .in1(vr1), .in2(vr2), .in3(vr3), .in4(vr4), .in5(vr5), .in6(vr6), .in7(vr7),
    .out(saidars1), .sel(rs1));
  Multiplexer #(.select(3), .width(18)) multiplexer_9 (
    .in0({18{1'b0}}), .in1(vr1), .in2(vr2), .in3(vr3), .in4(vr4), .in5(vr5), .in6(vr6), .in7(vr7),
    .out(saidars2), .sel(rs2));
  Multiplexer #(.select(3), .width(18)) multiplexer_10 (
    .in0({18{1'b0}}), .in1(vr1), .in2(vr2), .in3(vr3), .in4(vr4), .in5(vr5), .in6(vr6), .in7(vr7),
    .out(saidard), .sel(rd));

  // Notes on the sheet:
  //   r0
endmodule

module ULA (
  input  [17:0] rs1,
  input  [17:0] rs2,
  input  [17:0] rd,
  input  [2:0] opcodeula,
  output [17:0] out_5
);

  wire [4:0] bit_extender_1_out, bit_extender_2_out;
  wire [17:0] add, E, FMA, multiplier_1_out, OU, SHIFTLEFT, SHIFTRIGHT, sub, XORR;

  Adder #(.width(18)) adder_1 (.a(rs1), .b(rs2), .out(add));  // open: cin, cout
  assign E = rs1 & rs2;  // AND_Gate and_1, 18 bits wide
  assign OU = rs1 | rs2;  // OR_Gate or_1, 18 bits wide
  Multiplier #(.width(18)) multiplier_1 (.a(rs1), .b(rs2), .out(multiplier_1_out));  // open: cin, cout
  Bit_Extender #(.in_width(18), .out_width(5)) bit_extender_1 (.in(rs2), .out(bit_extender_1_out));
  Shifter #(.width(18)) shifter_1 (.in(rs1), .\dist (bit_extender_2_out), .out(SHIFTLEFT));
  Bit_Extender #(.in_width(18), .out_width(5)) bit_extender_2 (.in(rs2), .out(bit_extender_2_out));
  Subtractor #(.width(18)) subtractor_1 (.a(rs1), .b(rs2), .out(sub));  // open: bin, bout
  Adder #(.width(18)) adder_2 (.a(multiplier_1_out), .b(rd), .out(FMA));  // open: cin, cout
  Shifter #(.shift("ar"), .width(18)) shifter_2 (.in(rs1), .\dist (bit_extender_1_out), .out(SHIFTRIGHT));
  assign XORR = rs1 ^ rs2;  // XOR_Gate xor_1, 18 bits wide
  Multiplexer #(.select(3), .width(18)) multiplexer_1 (
    .in0(add), .in1(E), .in2(OU), .in3(FMA), .in4(SHIFTRIGHT), .in5(SHIFTLEFT), .in6(XORR), .in7(sub),
    .out(out_5), .sel(opcodeula));
endmodule
